// Logisim project Final Project Simulation.circ as structural Verilog: 8 circuits, main circuit main
module main (
  input  As,
  input  A1,
  input  A0,
  input  Bs,
  input  B1,
  input  B0,
  input  in_7,
  input  in_8,
  output Zero_Flag,
  output Div_By_Zero
);

  wire and_1_out, bcd_1_a_2, bcd_1_b_2, bcd_1_c_2, bcd_1_d_2, bcd_1_e, bcd_1_f, bcd_1_g, not_1_out;
  wire [5:1] multiplexer_1_out;
  wire [6:0] adding_and_subtracting_1_zero_flag, multiplying_1_zero_flag, reminder_1_zero;

  Reminder reminder_1 (
    .A0(A0), .A1(A1), .SA(As), .B0(B0), .B1(B1), .SB(Bs), .zero(reminder_1_zero[0]), .R0(reminder_1_zero[1]),
    .R1(reminder_1_zero[2]), .R2(reminder_1_zero[3]), .R3(reminder_1_zero[4]), .sign(reminder_1_zero[5]),
    .div_by_zero(reminder_1_zero[6]));
  Multiplying multiplying_1 (
    .A0(A0), .A1(A1), .SA(As), .B0(B0), .B1(B1), .SB(Bs), .ZERO_FLAG(multiplying_1_zero_flag[0]),
    .C0(multiplying_1_zero_flag[1]), .C1(multiplying_1_zero_flag[2]), .C2(multiplying_1_zero_flag[3]),
    .C3(multiplying_1_zero_flag[4]), .SIGN(multiplying_1_zero_flag[5]),
    .Div_By_Zero(multiplying_1_zero_flag[6]));
  Adding_and_Subtracting adding_and_subtracting_1 (
    .A0(A0), .A1(A1), .SA(As), .B0(B0), .B1(B1), .SB(Bs), .in_7(and_1_out),
    .ZERO_FLAG(adding_and_subtracting_1_zero_flag[0]), .C0(adding_and_subtracting_1_zero_flag[1]),
    .C1(adding_and_subtracting_1_zero_flag[2]), .C2(adding_and_subtracting_1_zero_flag[3]),
    .C3(adding_and_subtracting_1_zero_flag[4]), .SIGN(adding_and_subtracting_1_zero_flag[5]),
    .Div_By_Zero(adding_and_subtracting_1_zero_flag[6]));
  and and_1 (and_1_out, in_8, not_1_out);
  Multiplexer #(.select(2), .width(7), .enable("false")) multiplexer_1 (
    .in0(adding_and_subtracting_1_zero_flag), .in1(adding_and_subtracting_1_zero_flag),
    .in2(multiplying_1_zero_flag), .in3(reminder_1_zero), .out({Div_By_Zero, multiplexer_1_out, Zero_Flag}),
    .sel({in_7, in_8}));
  not not_1 (not_1_out, in_7);
  bcd bcd_1 (
    .D(multiplexer_1_out[4]), .C(multiplexer_1_out[3]), .B(multiplexer_1_out[2]), .A(multiplexer_1_out[1]),
    .Dv(Div_By_Zero), .e(bcd_1_e), .d_2(bcd_1_d_2), .c_2(bcd_1_c_2), .b_2(bcd_1_b_2), .a_2(bcd_1_a_2),
    .f(bcd_1_f), .g(bcd_1_g));
  _7_Segment_Display u_7_segment_display_1 (.g(multiplexer_1_out[5]));  // open: f, a, b, e, d, c, dp
  _7_Segment_Display u_7_segment_display_2 (
    .g(bcd_1_g), .f(bcd_1_f), .a(bcd_1_a_2), .b(bcd_1_b_2), .e(bcd_1_e), .d(bcd_1_d_2), .c(bcd_1_c_2));  // open: dp
endmodule

// REMIND
module Reminder (
  input  A0,
  input  A1,
  input  SA,
  input  B0,
  input  B1,
  input  SB,
  output zero,
  output R0,
  output R1,
  output R2,
  output R3,
  output sign,
  output div_by_zero
);

  wire nor_2_out, nor_3_out, not_1_out;

  R r_1 (.A1(A1), .A0(A0), .B1(B1), .B0(B0), .R1(R1), .R0(R0));
  nor nor_1 (div_by_zero, B1, B0);
  nor nor_2 (nor_2_out, R0, R1);
  and and_1 (zero, nor_2_out, not_1_out);
  not not_1 (not_1_out, div_by_zero);
  nor nor_3 (nor_3_out, zero, div_by_zero);
  and and_2 (sign, SA, nor_3_out);

  assign R2 = 1'b0;
  assign R3 = 1'b0;
endmodule

// MULT
module Multiplying (
  input  A0,
  input  A1,
  input  SA,
  input  B0,
  input  B1,
  input  SB,
  output ZERO_FLAG,
  output C0,
  output C1,
  output C2,
  output C3,
  output SIGN,
  output Div_By_Zero
);

  wire and_2_out, and_3_out, and_4_out, HF_c, or_1_out, or_2_out, or_3_out, xor_1_out;

  and and_1 (C0, A0, B0);
  and and_2 (and_2_out, A1, B0);
  and and_3 (and_3_out, A0, B1);
  and and_4 (and_4_out, B1, A1);
  xor xor_1 (xor_1_out, SA, SB);
  Half_Adder HF (.a(and_2_out), .b(and_3_out), .sum(C1), .c(HF_c));
  Half_Adder HF_2 (.a(and_4_out), .b(HF_c), .sum(C2), .c(C3));
  or or_1 (or_1_out, C2, C3);
  and and_5 (SIGN, xor_1_out, or_3_out);
  or or_2 (or_2_out, C0, C1);
  or or_3 (or_3_out, or_2_out, or_1_out);
  not not_1 (ZERO_FLAG, or_3_out);

  assign Div_By_Zero = 1'b0;
endmodule

module R (
  input  A1,
  input  A0,
  input  B1,
  input  B0,
  output R1,
  output R0
);

  wire and_1_out, and_2_out, and_4_out, nand_1_out, not_1_out;

  not not_1 (not_1_out, A0);
  and and_1 (and_1_out, A1, not_1_out);
  and and_2 (and_2_out, B1, B0);
  and and_3 (R1, and_1_out, and_2_out);
  and and_4 (and_4_out, B1, A0);
  nand nand_1 (nand_1_out, B0, A1);
  and and_5 (R0, and_4_out, nand_1_out);
endmodule

// HF
module Half_Adder (
  input  a,
  input  b,
  output sum,
  output c
);

  xor xor_1 (sum, a, b);
  and and_1 (c, a, b);
endmodule

// FA
module Full_Adder (
  input  a,
  input  b,
  input  cin,
  output sum,
  output C
);

  wire and_1_out, and_2_out, xor_1_out;

  xor xor_1 (xor_1_out, a, b);
  and and_1 (and_1_out, a, b);
  xor xor_2 (sum, xor_1_out, cin);
  and and_2 (and_2_out, xor_1_out, cin);
  or or_1 (C, and_2_out, and_1_out);
endmodule

// ADD & SUB
module Adding_and_Subtracting (
  input  A0,
  input  A1,
  input  SA,
  input  B0,
  input  B1,
  input  SB,
  input  in_7,
  output ZERO_FLAG,
  output C0,
  output C1,
  output C2,
  output C3,
  output SIGN,
  output Div_By_Zero
);

  wire and_1_out, full_adder_1_c, full_adder_1_sum, full_adder_2_c, full_adder_2_sum, half_adder_1_c,
       not_1_out, not_2_out, or_1_out, or_2_out, xor_1_out, xor_2_out, xor_3_out, xor_4_out, xor_5_out,
       xor_7_out, xor_8_out;

  xor xor_1 (xor_1_out, SB, in_7);
  xor xor_2 (xor_2_out, xor_1_out, SA);
  xor xor_3 (xor_3_out, xor_2_out, B0);
  xor xor_4 (xor_4_out, B1, xor_2_out);
  Full_Adder full_adder_1 (.a(A0), .b(xor_2_out), .cin(xor_3_out), .sum(full_adder_1_sum), .C(full_adder_1_c));
  Full_Adder full_adder_2 (.a(full_adder_1_c), .b(A1), .cin(xor_4_out), .sum(full_adder_2_sum), .C(full_adder_2_c));
  not not_1 (not_1_out, full_adder_2_c);
  not not_2 (not_2_out, xor_2_out);
  and and_1 (and_1_out, not_1_out, xor_2_out);
  and and_2 (C2, full_adder_2_c, not_2_out);
  xor xor_5 (xor_5_out, full_adder_1_sum, and_1_out);
  Half_Adder half_adder_1 (.a(xor_5_out), .b(and_1_out), .sum(C0), .c(half_adder_1_c));
  xor xor_6 (C1, half_adder_1_c, xor_7_out);
  xor xor_7 (xor_7_out, full_adder_2_sum, and_1_out);
  xor xor_8 (xor_8_out, and_1_out, SA);
  or or_1 (or_1_out, C0, C1);
  or or_2 (or_2_out, or_1_out, C2);
  not not_3 (ZERO_FLAG, or_2_out);
  and and_3 (SIGN, or_2_out, xor_8_out);

  assign C3 = 1'b0;
  assign Div_By_Zero = 1'b0;
endmodule

module bcd (
  input  D,
  input  C,
  input  B,
  input  A,
  input  Dv,
  output e,
  output d_2,
  output c_2,
  output b_2,
  output a_2,
  output f,
  output g
);

  wire and_1_out, and_2_out, and_3_out, and_4_out, and_5_out, and_6_out, and_7_out, and_8_out, and_9_out,
       and_10_out, and_11_out, and_12_out, and_13_out, and_14_out, and_15_out, and_16_out, and_17_out,
       not_1_out, not_2_out, not_3_out, not_4_out, not_5_out, not_6_out, not_7_out, not_8_out, not_9_out,
       not_10_out, not_11_out, not_12_out, not_13_out, not_14_out, not_15_out, not_16_out, not_17_out,
       not_18_out, not_19_out, not_20_out, not_21_out, not_22_out, not_23_out, not_24_out, not_25_out,
       not_26_out, not_27_out, not_28_out, not_29_out, not_30_out, not_31_out, not_32_out, or_1_out,
       or_2_out, or_4_out, or_5_out, or_6_out, or_7_out;

  not not_1 (not_1_out, C);
  not not_2 (not_2_out, A);
  not not_3 (not_3_out, A);
  not not_4 (not_4_out, C);
  not not_5 (not_5_out, A);
  not not_6 (not_6_out, Dv);
  not not_7 (not_7_out, C);
  not not_8 (not_8_out, Dv);
  not not_9 (not_9_out, A);
  not not_10 (not_10_out, Dv);
  not not_11 (not_11_out, B);
  not not_12 (not_12_out, Dv);
  not not_13 (not_13_out, Dv);
  not not_14 (not_14_out, B);
  not not_15 (not_15_out, B);
  not not_16 (not_16_out, A);
  not not_17 (not_17_out, C);
  not not_18 (not_18_out, A);
  not not_19 (not_19_out, B);
  not not_20 (not_20_out, A);
  not not_21 (not_21_out, B);
  not not_22 (not_22_out, A);
  not not_23 (not_23_out, C);
  not not_24 (not_24_out, B);
  not not_25 (not_25_out, A);
  and and_1 (and_1_out, not_1_out, not_2_out);
  and and_2 (and_2_out, B, not_3_out);
  and and_3 (and_3_out, not_4_out, not_5_out, not_6_out);
  and and_4 (and_4_out, not_7_out, B, not_8_out);
  and and_5 (and_5_out, B, not_9_out, not_10_out);
  and and_6 (and_6_out, C, not_11_out, A, not_12_out);
  and and_7 (and_7_out, D, not_13_out);
  not not_26 (not_26_out, Dv);
  or or_1 (or_1_out, not_14_out, A, C);
  not not_27 (not_27_out, C);
  and and_8 (and_8_out, not_15_out, not_16_out);
  and and_9 (and_9_out, B, A);
  and and_10 (and_10_out, not_17_out, not_18_out);
  and and_11 (and_11_out, C, A);
  and and_12 (and_12_out, not_19_out, not_20_out);
  and and_13 (and_13_out, C, not_21_out);
  and and_14 (and_14_out, C, not_22_out);
  and and_15 (and_15_out, not_23_out, B);
  and and_16 (and_16_out, C, not_24_out);
  and and_17 (and_17_out, C, not_25_out);
  not not_28 (not_28_out, Dv);
  and and_18 (e, not_28_out, or_2_out);
  or or_2 (or_2_out, and_1_out, and_2_out);
  or or_3 (d_2, and_3_out, and_4_out, and_5_out, and_6_out, and_7_out);
  and and_19 (c_2, not_26_out, or_1_out);
  not not_29 (not_29_out, Dv);
  and and_20 (b_2, not_29_out, or_4_out);
  or or_4 (or_4_out, not_27_out, and_8_out, and_9_out);
  not not_30 (not_30_out, Dv);
  or or_5 (or_5_out, and_10_out, B, and_11_out, D);
  not not_31 (not_31_out, Dv);
  or or_6 (or_6_out, and_12_out, and_13_out, and_14_out, D);
  not not_32 (not_32_out, Dv);
  or or_7 (or_7_out, and_15_out, and_16_out, and_17_out, D);
  and and_21 (a_2, not_30_out, or_5_out);
  and and_22 (f, not_31_out, or_6_out);
  and and_23 (g, not_32_out, or_7_out);
endmodule
